# Fritzing sketch Shield_v1-0 (saved by Fritzing 0.7.11b)
breadboards: 1

parts:
  Arduino = Arduino
  XBee = XBee
  10kΩ = 10k Ω Resistor [package=THT]
  15kΩ = 15k Ω Resistor [package=THT]
  Associate = LED - 5mm [color="Red (633nm)" package="5 mm [THT]"]
  1kΩ = Resistor [tolerance=±5% resistance=1k package=THT]
  PIN13 = LED - 5mm [color="Red (633nm)" package="5 mm [THT]"]
  1kΩ_2 = Resistor [tolerance=±5% resistance=1k package=THT]
  PIN12 = LED - 5mm [color="Red (633nm)" package="5 mm [THT]"]
  1KΩ = Resistor [tolerance=±5% resistance=1k package=THT]
  10kΩ_2 = Resistor [tolerance=±5% resistance=10k package=THT]
  DHT-22 = Humidity and Temperature Sensor RHT03

nets:
  GND: Arduino.GND, XBee.GND, 15kΩ.Pin_1, Associate.cathode, PIN13.cathode, PIN12.cathode, DHT-22.GND_2
  N1: Arduino.D13, 1kΩ_2.Pin_0
  N2: Arduino.D12, 1KΩ.Pin_0
  N3: Arduino.D2, 10kΩ_2.Pin_1, DHT-22.Data-signal
  N4: Arduino.D1TX, 10kΩ.Pin_0
  N5: Arduino.D0RX, XBee.pin2
  3V3: Arduino.3V3, XBee.VCC
  +5V: Arduino.+5V, 10kΩ_2.Pin_0, DHT-22.Vcc
  N6: XBee.pin3, 10kΩ.Pin_1, 15kΩ.Pin_0
  N7: XBee.pin5, 1kΩ.Pin_0
  N8: Associate.anode, 1kΩ.Pin_1
  N9: PIN13.anode, 1kΩ_2.Pin_1
  N10: PIN12.anode, 1KΩ.Pin_1

notes:
  Data Sensing Lab
  Babilim Light Industries
  Data Sensing Lab, DHT-22 XBee Arduino Shield, 1.0
